// Logisim project sqrt2.circ as structural Verilog: 22 circuits, main circuit main
module main (
  input  ENABLE,
  input  [15:0] IO_DATA_IN,
  output NAN,
  output PINF,
  output NINF,
  output RESULT,
  output [15:0] IO_DATA_OUT
);

  wire CLK_out;
  wire [11:0] sqrt_1_exp;

  Clock CLK (.out(CLK_out));
  sqrt sqrt_1 (
    .CLK(CLK_out), .ENABLE(ENABLE), .IO_DATA_IN(IO_DATA_IN), .IS_NAN(NAN), .IS_PINF(PINF), .IS_NINF(NINF),
    .RESULT(RESULT), .Exp(sqrt_1_exp));  // open: Res, out_10, out_11, IO_DATA_OUT, out_13, out_14, out_15, out_16
endmodule

module sqrt (
  input  CLK,
  input  ENABLE,
  input  [15:0] IO_DATA_IN,
  output IS_NAN,
  output IS_PINF,
  output IS_NINF,
  output RESULT,
  output [15:0] Res,
  output [11:0] Exp,
  output [11:0] out_10,
  output [11:0] out_11,
  output [15:0] IO_DATA_OUT,
  output [11:0] out_13,
  output [11:0] out_14,
  output [11:0] out_15,
  output [11:0] out_16
);

  wire and_1_out, and_2_out, comparator_1_res, comparator_2_res, if_is_nan_1_flag, if_is_neg_1_flag,
       if_is_zero_1_flag, not_2_out, parser_1_sign;
  wire [4:0] make_correct_exp_mant_1_res_exp, parser_1_exp;
  wire [9:0] parser_1_mant;
  wire [11:0] bit_extender_3_out, bit_extender_4_out, bit_extender_5_out, bit_extender_6_out,
       bit_extender_10_out, bit_extender_11_out, bit_extender_12_out, bit_extender_13_out,
       bit_extender_14_out, bit_extender_18_out, bit_extender_19_out, bit_extender_23_out,
       bit_extender_24_out, bit_extender_25_out, bit_extender_26_out, bit_extender_27_out,
       make_correct_exp_mant_1_res_mant, substractor_1_res, substractor_2_res, summator_1_sum,
       summator_2_sum, summator_3_sum, summator_4_sum, summator_5_sum, summator_6_sum;
  wire [15:0] bit_extender_1_out, bit_extender_2_out, bit_extender_7_out, bit_extender_8_out,
       bit_extender_9_out, bit_extender_15_out, bit_extender_16_out, bit_extender_17_out,
       bit_extender_20_out, bit_extender_21_out, bit_extender_22_out, bit_extender_28_out,
       bit_extender_30_out, bit_extender_31_out, bit_shift_left_1_out_2, bit_shift_left_2_out_2,
       bit_shift_left_3_out_2, bit_shift_left_4_out_2, bit_shift_left_5_out_2, bit_shift_left_6_out_2,
       bit_shift_left_7_out_2, bit_shift_left_8_out_2, bit_shift_left_9_out_2, bit_shift_left_10_out_2,
       bit_shift_left_11_out_2, bit_shift_left_12_out_2, counter_1_res, if_else_expression_2_res,
       if_else_expression_3_res, if_else_expression_4_res, if_else_expression_5_res,
       if_else_expression_6_res, if_else_expression_7_res, if_else_expression_8_res,
       if_else_expression_9_res, if_is_nan_1_res, if_is_neg_1_res, if_is_pinf_1_res, if_is_zero_1_res,
       not_1_out, pull_resistor_1_node, rest_if_res, result_if_res;

  counter counter_1 (.C(CLK), .Enable(ENABLE), .Res(counter_1_res));
  parser parser_1 (.HP_num(pull_resistor_1_node), .Mant(parser_1_mant), .Exp(parser_1_exp), .Sign(parser_1_sign));
  Pull_Resistor pull_resistor_1 (.node(pull_resistor_1_node));
  Transistor #(.width(16)) transistor_1 (.in(IO_DATA_IN), .out(pull_resistor_1_node), .gate(not_1_out));
  and and_1 (and_1_out, ~counter_1_res[0], ~counter_1_res[1], ~counter_1_res[2], ~counter_1_res[3], ~counter_1_res[4], ~counter_1_res[5], ~counter_1_res[6], ~counter_1_res[7], ~counter_1_res[8], ~counter_1_res[9], ~counter_1_res[10], ~counter_1_res[11], ~counter_1_res[12], ~counter_1_res[13], ~counter_1_res[14], ~counter_1_res[15]);  // AND_Gate
  not not_1 (not_1_out[0], and_1_out);
  if_is_zero if_is_zero_1 (
    .Mant(parser_1_mant), .Exp(parser_1_exp), .Sign(parser_1_sign), .Flag(if_is_zero_1_flag),
    .Res(if_is_zero_1_res));
  if_is_pinf if_is_pinf_1 (
    .Mant(parser_1_mant), .Exp(parser_1_exp), .Sign(parser_1_sign), .Flag(IS_PINF), .Res(if_is_pinf_1_res));
  if_is_nan if_is_nan_1 (
    .Mant(parser_1_mant), .Exp(parser_1_exp), .Sign(parser_1_sign), .Flag(if_is_nan_1_flag),
    .Res(if_is_nan_1_res));
  if_is_neg if_is_neg_1 (
    .Mant(parser_1_mant), .Exp(parser_1_exp), .Sign(parser_1_sign), .Flag(if_is_neg_1_flag),
    .Res(if_is_neg_1_res));
  make_correct_exp_mant make_correct_exp_mant_1 (
    .Mant(parser_1_mant), .Exp(parser_1_exp), .Res_mant(make_correct_exp_mant_1_res_mant),
    .Res_exp(make_correct_exp_mant_1_res_exp));
  or or_1 (RESULT, IS_PINF, if_is_zero_1_flag, if_is_nan_1_flag, if_is_neg_1_flag);
  assign bit_extender_1_out = {{4{1'b0}}, make_correct_exp_mant_1_res_mant};  // Bit_Extender bit_extender_1
  assign bit_extender_2_out = {{4{1'b0}}, bit_extender_26_out};  // Bit_Extender bit_extender_2
  if_else_expression if_else_expression_1 (
    .expression(if_is_zero_1_flag), .value_1(if_is_zero_1_res), .value_2(if_else_expression_2_res), .res(Res));
  if_else_expression if_else_expression_2 (
    .expression(IS_PINF), .value_1(if_is_pinf_1_res), .value_2(if_else_expression_3_res),
    .res(if_else_expression_2_res));
  if_else_expression if_else_expression_3 (
    .expression(if_is_nan_1_flag), .value_1(if_is_nan_1_res), .value_2(if_else_expression_4_res),
    .res(if_else_expression_3_res));
  if_else_expression if_else_expression_4 (
    .expression(if_is_neg_1_flag), .value_1(if_is_neg_1_res), .value_2({16{1'b0}}),
    .res(if_else_expression_4_res));
  if_else_expression if_else_expression_5 (
    .expression(and_1_out), .value_1({16{1'b0}}), .value_2(result_if_res), .res(if_else_expression_5_res));
  or or_2 (IS_NAN, if_is_nan_1_flag, if_is_neg_1_flag);
  assign bit_extender_3_out = {{7{1'b0}}, make_correct_exp_mant_1_res_exp};  // Bit_Extender bit_extender_3
  and and_2 (and_2_out, and_1_out, CLK);
  Bit_Extender #(.in_width(16), .out_width(12), .\type ("zero")) bit_extender_4 (
    .in(if_else_expression_5_res), .out(bit_extender_4_out));
  Bit_Extender #(.in_width(16), .out_width(12), .\type ("zero")) bit_extender_5 (
    .in(if_else_expression_6_res), .out(bit_extender_5_out));
  if_else_expression if_else_expression_6 (
    .expression(and_1_out), .value_1({16{1'b0}}), .value_2(rest_if_res), .res(if_else_expression_6_res));
  Bit_Extender #(.in_width(16), .out_width(12), .\type ("zero")) bit_extender_6 (
    .in(if_else_expression_7_res), .out(bit_extender_6_out));
  if_else_expression if_else_expression_7 (
    .expression(and_1_out), .value_1(bit_extender_1_out), .value_2(bit_extender_2_out),
    .res(if_else_expression_7_res));
  memory memory_1 (.A(bit_extender_3_out), .C(and_2_out), .Enable(ENABLE), .Res(Exp));
  memory num1 (.A(bit_extender_6_out), .C(CLK), .Enable(ENABLE), .Res(out_10));
  memory rest1 (.A(bit_extender_5_out), .C(CLK), .Enable(ENABLE), .Res(out_13));
  memory result1 (.A(bit_extender_4_out), .C(CLK), .Enable(ENABLE), .Res(out_15));
  assign bit_extender_7_out = {{4{1'b0}}, out_10};  // Bit_Extender bit_extender_7
  assign bit_extender_8_out = {{4{1'b0}}, out_13};  // Bit_Extender bit_extender_8
  assign bit_extender_9_out = {{4{1'b0}}, out_15};  // Bit_Extender bit_extender_9
  bit_shift_left bit_shift_left_1 (.in_1(bit_extender_7_out), .out_2(bit_shift_left_1_out_2));
  bit_shift_left bit_shift_left_2 (.in_1(bit_extender_8_out), .out_2(bit_shift_left_2_out_2));
  bit_shift_left bit_shift_left_3 (.in_1(bit_extender_9_out), .out_2(bit_shift_left_3_out_2));
  not not_2 (not_2_out, CLK);
  Bit_Extender #(.in_width(16), .out_width(12), .\type ("zero")) bit_extender_10 (
    .in(bit_shift_left_3_out_2), .out(bit_extender_10_out));
  Bit_Extender #(.in_width(16), .out_width(12), .\type ("zero")) bit_extender_11 (
    .in(bit_shift_left_4_out_2), .out(bit_extender_11_out));
  bit_shift_left bit_shift_left_4 (.in_1(bit_shift_left_1_out_2), .out_2(bit_shift_left_4_out_2));
  Bit_Extender #(.in_width(16), .out_width(12), .\type ("zero")) bit_extender_12 (
    .in(bit_shift_left_5_out_2), .out(bit_extender_12_out));
  bit_shift_left bit_shift_left_5 (.in_1(bit_shift_left_2_out_2), .out_2(bit_shift_left_5_out_2));
  Bit_Extender #(.in_width(16), .out_width(12), .\type ("zero")) bit_extender_13 (
    .in(bit_shift_left_6_out_2), .out(bit_extender_13_out));
  bit_shift_left bit_shift_left_6 (.in_1(bit_shift_left_3_out_2), .out_2(bit_shift_left_6_out_2));
  assign bit_extender_14_out = {{10{1'b0}}, out_10[11:10]};  // Bit_Extender bit_extender_14
  summator summator_1 (.B(bit_extender_13_out), .A(12'h1), .Sum(summator_1_sum));
  summator summator_2 (.B(12'h1), .A(bit_extender_10_out), .Sum(summator_2_sum));
  assign bit_extender_15_out = {{4{1'b0}}, summator_2_sum};  // Bit_Extender bit_extender_15
  summator summator_3 (.B(bit_extender_12_out), .A(bit_extender_14_out), .Sum(summator_3_sum));
  comparator comparator_1 (.B(summator_1_sum), .A(summator_3_sum), .res(comparator_1_res));
  substractor substractor_1 (.B(summator_1_sum), .A(summator_3_sum), .Res(substractor_1_res));  // open: is_neg
  assign bit_extender_16_out = {{4{1'b0}}, summator_3_sum};  // Bit_Extender bit_extender_16
  assign bit_extender_17_out = {{4{1'b0}}, substractor_1_res};  // Bit_Extender bit_extender_17
  if_else_expression if_else_expression_8 (
    .expression(comparator_1_res), .value_1(bit_extender_15_out), .value_2(bit_shift_left_3_out_2),
    .res(if_else_expression_8_res));
  if_else_expression if_else_expression_9 (
    .expression(comparator_1_res), .value_1(bit_extender_17_out), .value_2(bit_extender_16_out),
    .res(if_else_expression_9_res));
  Bit_Extender #(.in_width(16), .out_width(12), .\type ("zero")) bit_extender_18 (
    .in(if_else_expression_8_res), .out(bit_extender_18_out));
  Bit_Extender #(.in_width(16), .out_width(12), .\type ("zero")) bit_extender_19 (
    .in(if_else_expression_9_res), .out(bit_extender_19_out));
  memory num2 (.A(bit_extender_11_out), .C(not_2_out), .Enable(ENABLE), .Res(out_11));
  memory rest2 (.A(bit_extender_19_out), .C(not_2_out), .Enable(ENABLE), .Res(out_14));
  memory result2 (.A(bit_extender_18_out), .C(not_2_out), .Enable(ENABLE), .Res(out_16));
  assign bit_extender_20_out = {{4{1'b0}}, out_11};  // Bit_Extender bit_extender_20
  assign bit_extender_21_out = {{4{1'b0}}, out_14};  // Bit_Extender bit_extender_21
  assign bit_extender_22_out = {{4{1'b0}}, out_16};  // Bit_Extender bit_extender_22
  bit_shift_left bit_shift_left_7 (.in_1(bit_extender_20_out), .out_2(bit_shift_left_7_out_2));
  bit_shift_left bit_shift_left_8 (.in_1(bit_extender_21_out), .out_2(bit_shift_left_8_out_2));
  bit_shift_left bit_shift_left_9 (.in_1(bit_extender_22_out), .out_2(bit_shift_left_9_out_2));
  bit_shift_left bit_shift_left_10 (.in_1(bit_shift_left_7_out_2), .out_2(bit_shift_left_10_out_2));
  Bit_Extender #(.in_width(16), .out_width(12), .\type ("zero")) bit_extender_23 (
    .in(bit_shift_left_11_out_2), .out(bit_extender_23_out));
  bit_shift_left bit_shift_left_11 (.in_1(bit_shift_left_8_out_2), .out_2(bit_shift_left_11_out_2));
  Bit_Extender #(.in_width(16), .out_width(12), .\type ("zero")) bit_extender_24 (
    .in(bit_shift_left_12_out_2), .out(bit_extender_24_out));
  bit_shift_left bit_shift_left_12 (.in_1(bit_shift_left_9_out_2), .out_2(bit_shift_left_12_out_2));
  assign bit_extender_25_out = {{10{1'b0}}, out_11[11:10]};  // Bit_Extender bit_extender_25
  Bit_Extender #(.in_width(16), .out_width(12), .\type ("zero")) bit_extender_26 (
    .in(bit_shift_left_10_out_2), .out(bit_extender_26_out));
  Bit_Extender #(.in_width(16), .out_width(12), .\type ("zero")) bit_extender_27 (
    .in(bit_shift_left_9_out_2), .out(bit_extender_27_out));
  summator summator_4 (.B(12'h1), .A(bit_extender_27_out), .Sum(summator_4_sum));
  assign bit_extender_28_out = {{4{1'b0}}, summator_4_sum};  // Bit_Extender bit_extender_28
  summator summator_5 (.B(bit_extender_24_out), .A(12'h1), .Sum(summator_5_sum));
  summator summator_6 (.B(bit_extender_23_out), .A(bit_extender_25_out), .Sum(summator_6_sum));
  comparator comparator_2 (.B(summator_5_sum), .A(summator_6_sum), .res(comparator_2_res));
  Bit_Extender #(.in_width(12), .\type ("zero")) bit_extender_29 (.in(summator_6_sum));  // open: out
  substractor substractor_2 (.B(summator_5_sum), .A(summator_6_sum), .Res(substractor_2_res));  // open: is_neg
  assign bit_extender_30_out = {{4{1'b0}}, summator_6_sum};  // Bit_Extender bit_extender_30
  assign bit_extender_31_out = {{4{1'b0}}, substractor_2_res};  // Bit_Extender bit_extender_31
  if_else_expression result_if (
    .expression(comparator_2_res), .value_1(bit_extender_28_out), .value_2(bit_shift_left_9_out_2),
    .res(result_if_res));
  if_else_expression rest_if (
    .expression(comparator_2_res), .value_1(bit_extender_31_out), .value_2(bit_extender_30_out),
    .res(rest_if_res));
  // Pins of 1 and 16 bits meet at not_1_out

  assign IO_DATA_OUT = IO_DATA_IN;
  assign IS_NINF = 1'b0;
endmodule

module bit_summator (
  input  A,
  input  B,
  input  extra,
  output Sum,
  output res_extra
);

  wire and_1_out, and_2_out, xor_1_out;

  xor xor_1 (xor_1_out, A, B);
  and and_1 (and_1_out, A, B);
  and and_2 (and_2_out, xor_1_out, extra);
  xor xor_2 (Sum, xor_1_out, extra);
  or or_1 (res_extra, and_2_out, and_1_out);
endmodule

module summator (
  input  [11:0] B,
  input  [11:0] A,
  output [11:0] Sum
);

  wire bit_summator_1_res_extra, bit_summator_2_res_extra, bit_summator_3_res_extra,
       bit_summator_4_res_extra, bit_summator_5_res_extra, bit_summator_6_res_extra,
       bit_summator_7_res_extra, bit_summator_8_res_extra, bit_summator_9_res_extra,
       bit_summator_10_res_extra, bit_summator_11_res_extra;

  bit_summator bit_summator_1 (.A(A[0]), .B(B[0]), .extra(1'b0), .Sum(Sum[0]), .res_extra(bit_summator_1_res_extra));
  bit_summator bit_summator_2 (
    .A(A[1]), .B(B[1]), .extra(bit_summator_1_res_extra), .Sum(Sum[1]), .res_extra(bit_summator_2_res_extra));
  bit_summator bit_summator_3 (
    .A(A[2]), .B(B[2]), .extra(bit_summator_2_res_extra), .Sum(Sum[2]), .res_extra(bit_summator_3_res_extra));
  bit_summator bit_summator_4 (
    .A(A[3]), .B(B[3]), .extra(bit_summator_3_res_extra), .Sum(Sum[3]), .res_extra(bit_summator_4_res_extra));
  bit_summator bit_summator_5 (
    .A(A[4]), .B(B[4]), .extra(bit_summator_4_res_extra), .Sum(Sum[4]), .res_extra(bit_summator_5_res_extra));
  bit_summator bit_summator_6 (
    .A(A[5]), .B(B[5]), .extra(bit_summator_5_res_extra), .Sum(Sum[5]), .res_extra(bit_summator_6_res_extra));
  bit_summator bit_summator_7 (
    .A(A[6]), .B(B[6]), .extra(bit_summator_6_res_extra), .Sum(Sum[6]), .res_extra(bit_summator_7_res_extra));
  bit_summator bit_summator_8 (
    .A(A[7]), .B(B[7]), .extra(bit_summator_7_res_extra), .Sum(Sum[7]), .res_extra(bit_summator_8_res_extra));
  bit_summator bit_summator_9 (
    .A(A[8]), .B(B[8]), .extra(bit_summator_8_res_extra), .Sum(Sum[8]), .res_extra(bit_summator_9_res_extra));
  bit_summator bit_summator_10 (
    .A(A[9]), .B(B[9]), .extra(bit_summator_9_res_extra), .Sum(Sum[9]), .res_extra(bit_summator_10_res_extra));
  bit_summator bit_summator_11 (
    .A(A[10]), .B(B[10]), .extra(bit_summator_10_res_extra), .Sum(Sum[10]),
    .res_extra(bit_summator_11_res_extra));
  bit_summator bit_summator_12 (
    .A(A[11]), .B(B[11]), .extra(bit_summator_11_res_extra), .Sum(Sum[11]));  // open: res_extra
endmodule

module bit_substractor (
  input  A,
  input  B,
  input  Borrow_in,
  output Diff,
  output Borrow_out
);

  wire and_1_out, and_2_out, not_1_out, not_2_out, xor_1_out;

  not not_1 (not_1_out, A);
  xor xor_1 (xor_1_out, A, B);
  and and_1 (and_1_out, not_1_out, B);
  not not_2 (not_2_out, xor_1_out);
  xor xor_2 (Diff, xor_1_out, Borrow_in);
  and and_2 (and_2_out, Borrow_in, not_2_out);
  or or_1 (Borrow_out, and_2_out, and_1_out);
endmodule

module bit_shift_left (
  input  [15:0] in_1,
  output [15:0] out_2
);


  assign out_2 = {in_1[14:0], 1'b0};
endmodule

module substractor (
  input  [11:0] B,
  input  [11:0] A,
  output [11:0] Res,
  output is_neg
);

  wire bit_substractor_1_borrow_out, bit_substractor_2_borrow_out, bit_substractor_3_borrow_out,
       bit_substractor_4_borrow_out, bit_substractor_5_borrow_out, bit_substractor_6_borrow_out,
       bit_substractor_7_borrow_out, bit_substractor_8_borrow_out, bit_substractor_9_borrow_out,
       bit_substractor_10_borrow_out, bit_substractor_11_borrow_out;

  bit_substractor bit_substractor_1 (
    .A(A[0]), .B(B[0]), .Borrow_in(1'b0), .Diff(Res[0]), .Borrow_out(bit_substractor_1_borrow_out));
  bit_substractor bit_substractor_2 (
    .A(A[1]), .B(B[1]), .Borrow_in(bit_substractor_1_borrow_out), .Diff(Res[1]),
    .Borrow_out(bit_substractor_2_borrow_out));
  bit_substractor bit_substractor_3 (
    .A(A[2]), .B(B[2]), .Borrow_in(bit_substractor_2_borrow_out), .Diff(Res[2]),
    .Borrow_out(bit_substractor_3_borrow_out));
  bit_substractor bit_substractor_4 (
    .A(A[3]), .B(B[3]), .Borrow_in(bit_substractor_3_borrow_out), .Diff(Res[3]),
    .Borrow_out(bit_substractor_4_borrow_out));
  bit_substractor bit_substractor_5 (
    .A(A[4]), .B(B[4]), .Borrow_in(bit_substractor_4_borrow_out), .Diff(Res[4]),
    .Borrow_out(bit_substractor_5_borrow_out));
  bit_substractor bit_substractor_6 (
    .A(A[5]), .B(B[5]), .Borrow_in(bit_substractor_5_borrow_out), .Diff(Res[5]),
    .Borrow_out(bit_substractor_6_borrow_out));
  bit_substractor bit_substractor_7 (
    .A(A[6]), .B(B[6]), .Borrow_in(bit_substractor_6_borrow_out), .Diff(Res[6]),
    .Borrow_out(bit_substractor_7_borrow_out));
  bit_substractor bit_substractor_8 (
    .A(A[7]), .B(B[7]), .Borrow_in(bit_substractor_7_borrow_out), .Diff(Res[7]),
    .Borrow_out(bit_substractor_8_borrow_out));
  bit_substractor bit_substractor_9 (
    .A(A[8]), .B(B[8]), .Borrow_in(bit_substractor_8_borrow_out), .Diff(Res[8]),
    .Borrow_out(bit_substractor_9_borrow_out));
  bit_substractor bit_substractor_10 (
    .A(A[9]), .B(B[9]), .Borrow_in(bit_substractor_9_borrow_out), .Diff(Res[9]),
    .Borrow_out(bit_substractor_10_borrow_out));
  bit_substractor bit_substractor_11 (
    .A(A[10]), .B(B[10]), .Borrow_in(bit_substractor_10_borrow_out), .Diff(Res[10]),
    .Borrow_out(bit_substractor_11_borrow_out));
  bit_substractor bit_substractor_12 (
    .A(A[11]), .B(B[11]), .Borrow_in(bit_substractor_11_borrow_out), .Diff(Res[11]), .Borrow_out(is_neg));
endmodule

module rs_trigger_sync (
  input  R,
  input  C,
  input  S,
  input  Enable,
  output Q,
  output NQ
);

  wire and_1_out, and_2_out, nor_2_out, not_1_out, or_1_out, por_1_out;

  not not_1 (not_1_out, Enable);
  and and_1 (and_1_out, R, C);
  and and_2 (and_2_out, C, S);
  POR por_1 (.out(por_1_out));
  or or_1 (or_1_out, not_1_out, por_1_out);
  nor nor_1 (Q, and_1_out, NQ);
  nor nor_2 (nor_2_out, Q, and_2_out);
  or or_2 (NQ, nor_2_out, or_1_out);
endmodule

module d_trigger (
  input  D,
  input  C,
  input  Enable,
  output Q,
  output NQ
);

  wire not_1_out;

  not not_1 (not_1_out, D);
  rs_trigger_sync rs_trigger_sync_1 (.R(not_1_out), .C(C), .S(D), .Enable(Enable), .Q(Q), .NQ(NQ));
endmodule

module bigger_equal_comp (
  input  A,
  input  B,
  output Equal,
  output Bigger
);

  wire and_1_out, and_2_out;

  and and_1 (and_1_out, A, B);
  and and_2 (and_2_out, ~A, ~B);  // AND_Gate
  and and_3 (Bigger, A, ~B);  // AND_Gate
  or or_1 (Equal, and_1_out, and_2_out);
endmodule

module comparator (
  input  [11:0] B,
  input  [11:0] A,
  output res
);

  wire substractor_1_is_neg;

  substractor substractor_1 (.B(B), .A(A), .is_neg(substractor_1_is_neg));  // open: Res
  not not_1 (res, substractor_1_is_neg);
endmodule

module parser (
  input  [15:0] HP_num,
  output [9:0] Mant,
  output [4:0] Exp,
  output Sign
);


  assign Exp = HP_num[14:10];
  assign Mant = HP_num[9:0];
  assign Sign = HP_num[15];
endmodule

module if_is_zero (
  input  [9:0] Mant,
  input  [4:0] Exp,
  input  Sign,
  output Flag,
  output [15:0] Res
);

  wire and_1_out;

  and and_1 (and_1_out, ~Mant[0], ~Mant[1], ~Mant[2], ~Mant[3], ~Mant[4], ~Mant[5], ~Mant[6], ~Mant[7], ~Mant[8], ~Mant[9], ~Exp[0], ~Exp[1], ~Exp[2], ~Exp[3], ~Exp[4]);  // AND_Gate
  and and_2 (Flag, and_1_out, Sign);

  assign Res = {1'b0, Exp, Mant};
endmodule

module if_is_nan (
  input  [9:0] Mant,
  input  [4:0] Exp,
  input  Sign,
  output Flag,
  output [15:0] Res
);

  wire and_1_out, or_1_out;

  or or_1 (or_1_out, Mant[0], Mant[1], Mant[2], Mant[3], Mant[4], Mant[5], Mant[6], Mant[7], Mant[8], Mant[9]);
  and and_1 (and_1_out, Exp[0], Exp[1], Exp[2], Exp[3], Exp[4]);
  and and_2 (Flag, or_1_out, and_1_out);

  assign Res = {Sign, Exp, Mant};
endmodule

module if_is_pinf (
  input  [9:0] Mant,
  input  [4:0] Exp,
  input  Sign,
  output Flag,
  output [15:0] Res
);

  and and_1 (Flag, ~Mant[0], ~Mant[1], ~Mant[2], ~Mant[3], ~Mant[4], ~Mant[5], ~Mant[6], ~Mant[7], ~Mant[8], ~Mant[9], Exp[0], Exp[1], Exp[2], Exp[3], Exp[4], ~Sign);  // AND_Gate

  assign Res = {Sign, Exp, Mant};
endmodule

module if_is_neg (
  input  [9:0] Mant,
  input  [4:0] Exp,
  input  Sign,
  output Flag,
  output [15:0] Res
);

  wire if_is_nan_1_flag, if_is_zero_1_flag;

  if_is_zero if_is_zero_1 (.Mant(Mant), .Exp(Exp), .Flag(if_is_zero_1_flag));  // open: Sign, Res
  if_is_nan if_is_nan_1 (.Mant(Mant), .Exp(Exp), .Sign(Sign), .Flag(if_is_nan_1_flag));  // open: Res
  and and_1 (Flag, ~if_is_zero_1_flag, ~if_is_nan_1_flag, Sign);  // AND_Gate

  assign Res = 16'hfe00;
endmodule

module if_else_expression (
  input  expression,
  input  [15:0] value_1,
  input  [15:0] value_2,
  output [15:0] res
);

  wire not_1_out;

  not not_1 (not_1_out, expression);
  Transistor #(.\type ("n"), .width(16)) transistor_1 (.in(value_2), .out(res), .gate(not_1_out));
  Transistor #(.\type ("n"), .width(16)) transistor_2 (.in(value_1), .out(res), .gate(expression));
  Pull_Resistor #(.pull(1)) pull_resistor_1 (.node(res));
endmodule

module memory (
  input  [11:0] A,
  input  C,
  input  Enable,
  output [11:0] Res
);

  d_trigger d_trigger_1 (.D(A[0]), .C(C), .Enable(Enable), .Q(Res[0]));  // open: NQ
  d_trigger d_trigger_2 (.D(A[1]), .C(C), .Enable(Enable), .Q(Res[1]));  // open: NQ
  d_trigger d_trigger_3 (.D(A[2]), .C(C), .Enable(Enable), .Q(Res[2]));  // open: NQ
  d_trigger d_trigger_4 (.D(A[3]), .C(C), .Enable(Enable), .Q(Res[3]));  // open: NQ
  d_trigger d_trigger_5 (.D(A[4]), .C(C), .Enable(Enable), .Q(Res[4]));  // open: NQ
  d_trigger d_trigger_6 (.D(A[5]), .C(C), .Enable(Enable), .Q(Res[5]));  // open: NQ
  d_trigger d_trigger_7 (.D(A[6]), .C(C), .Enable(Enable), .Q(Res[6]));  // open: NQ
  d_trigger d_trigger_8 (.D(A[7]), .C(C), .Enable(Enable), .Q(Res[7]));  // open: NQ
  d_trigger d_trigger_9 (.D(A[8]), .C(C), .Enable(Enable), .Q(Res[8]));  // open: NQ
  d_trigger d_trigger_10 (.D(A[9]), .C(C), .Enable(Enable), .Q(Res[9]));  // open: NQ
  d_trigger d_trigger_11 (.D(A[10]), .C(C), .Enable(Enable), .Q(Res[10]));  // open: NQ
  d_trigger d_trigger_12 (.D(A[11]), .C(C), .Enable(Enable), .Q(Res[11]));  // open: NQ
endmodule

module make_correct_exp_mant (
  input  [9:0] Mant,
  input  [4:0] Exp,
  output [11:0] Res_mant,
  output [4:0] Res_exp
);

  wire comparator_1_res;
  wire [11:0] bit_extender_4_out, bit_extender_5_out, substractor_1_res, substractor_2_res,
       substractor_3_res, substractor_4_res, summator_1_sum;
  wire [15:0] bit_extender_1_out, bit_extender_2_out, bit_extender_6_out, bit_extender_7_out,
       bit_shift_left_1_out_2, bit_shift_right_1_out_2, bit_shift_right_2_out_2, if_else_expression_2_res,
       if_else_expression_3_res;
  wire [15:12] if_else_expression_1_res;

  bit_shift_left bit_shift_left_1 (.in_1({6'b000001, Mant}), .out_2(bit_shift_left_1_out_2));
  substractor substractor_1 (.B(12'h1), .A({{7{1'b0}}, Exp}), .Res(substractor_1_res));  // open: is_neg
  if_else_expression if_else_expression_1 (
    .expression(Exp[0]), .value_1({6'b000001, Mant}), .value_2(bit_shift_left_1_out_2),
    .res({if_else_expression_1_res, Res_mant}));
  if_else_expression if_else_expression_2 (
    .expression(Exp[0]), .value_1({{11{1'b0}}, Exp}), .value_2({4'b0000, substractor_1_res}),
    .res(if_else_expression_2_res));
  comparator comparator_1 (.B(if_else_expression_2_res[11:0]), .A(12'he), .res(comparator_1_res));
  assign bit_extender_1_out = {{4{1'b0}}, substractor_2_res};  // Bit_Extender bit_extender_1
  substractor substractor_2 (.B(if_else_expression_2_res[11:0]), .A(12'hf), .Res(substractor_2_res));  // open: is_neg
  assign bit_extender_2_out = {{4{1'b0}}, substractor_3_res};  // Bit_Extender bit_extender_2
  substractor substractor_3 (.B(12'hf), .A(if_else_expression_2_res[11:0]), .Res(substractor_3_res));  // open: is_neg
  if_else_expression if_else_expression_3 (
    .expression(comparator_1_res), .value_1(bit_extender_6_out), .value_2(bit_extender_7_out),
    .res(if_else_expression_3_res));
  bit_shift_right bit_shift_right_1 (.in_1(bit_extender_1_out), .out_2(bit_shift_right_1_out_2));
  bit_shift_right bit_shift_right_2 (.in_1(bit_extender_2_out), .out_2(bit_shift_right_2_out_2));
  Bit_Extender #(.in_width(16), .out_width(5), .\type ("zero")) bit_extender_3 (
    .in(if_else_expression_3_res), .out(Res_exp));
  Bit_Extender #(.in_width(16), .out_width(12), .\type ("zero")) bit_extender_4 (
    .in(bit_shift_right_1_out_2), .out(bit_extender_4_out));
  Bit_Extender #(.in_width(16), .out_width(12), .\type ("zero")) bit_extender_5 (
    .in(bit_shift_right_2_out_2), .out(bit_extender_5_out));
  assign bit_extender_6_out = {{4{1'b0}}, substractor_4_res};  // Bit_Extender bit_extender_6
  substractor substractor_4 (.B(bit_extender_4_out), .A(12'hf), .Res(substractor_4_res));  // open: is_neg
  assign bit_extender_7_out = {{4{1'b0}}, summator_1_sum};  // Bit_Extender bit_extender_7
  summator summator_1 (.B(bit_extender_5_out), .A(12'hf), .Sum(summator_1_sum));
endmodule

module jk_trigger_sync (
  input  K,
  input  C,
  input  J,
  input  Enable,
  output Q,
  output NQ
);

  wire and_1_out, and_2_out, not_1_out, rs_trigger_sync_1_nq, rs_trigger_sync_1_q;

  and and_1 (and_1_out, Q, K);
  and and_2 (and_2_out, J, NQ);
  not not_1 (not_1_out, C);
  rs_trigger_sync rs_trigger_sync_1 (
    .R(and_1_out), .C(C), .S(and_2_out), .Enable(Enable), .Q(rs_trigger_sync_1_q), .NQ(rs_trigger_sync_1_nq));
  rs_trigger_sync rs_trigger_sync_2 (
    .R(rs_trigger_sync_1_nq), .C(not_1_out), .S(rs_trigger_sync_1_q), .Enable(Enable), .Q(Q), .NQ(NQ));
endmodule

module counter (
  input  C,
  input  Enable,
  output [15:0] Res
);

  wire jk_trigger_sync_1_nq, jk_trigger_sync_1_q, jk_trigger_sync_2_nq, jk_trigger_sync_2_q,
       jk_trigger_sync_3_nq, jk_trigger_sync_3_q, jk_trigger_sync_4_nq;

  jk_trigger_sync jk_trigger_sync_1 (
    .K(Enable), .C(C), .J(Enable), .Enable(Enable), .Q(jk_trigger_sync_1_q), .NQ(jk_trigger_sync_1_nq));
  jk_trigger_sync jk_trigger_sync_2 (
    .K(Enable), .C(jk_trigger_sync_1_q), .J(Enable), .Enable(Enable), .Q(jk_trigger_sync_2_q),
    .NQ(jk_trigger_sync_2_nq));
  jk_trigger_sync jk_trigger_sync_3 (
    .K(Enable), .C(jk_trigger_sync_2_q), .J(Enable), .Enable(Enable), .Q(jk_trigger_sync_3_q),
    .NQ(jk_trigger_sync_3_nq));
  jk_trigger_sync jk_trigger_sync_4 (
    .K(Enable), .C(jk_trigger_sync_3_q), .J(Enable), .Enable(Enable), .NQ(jk_trigger_sync_4_nq));  // open: Q
  not not_1 (Res[3], jk_trigger_sync_4_nq);
  not not_2 (Res[2], jk_trigger_sync_3_nq);
  not not_3 (Res[1], jk_trigger_sync_2_nq);
  not not_4 (Res[0], jk_trigger_sync_1_nq);

  assign Res[15:4] = {12{1'b0}};
endmodule

module bit_shift_right (
  input  [15:0] in_1,
  output [15:0] out_2
);


  assign out_2 = {1'b0, in_1[15:1]};
endmodule
